# Fritzing sketch KegScale (saved by Fritzing 1.0.7)
breadboards: 1

parts:
  Part2 = HX711 Weighing Sensor Module
  S1 = Load Sensor - 50kg [part_number=SEN-10245]
  S2 = Load Sensor - 50kg [part_number=SEN-10245]
  S3 = Load Sensor - 50kg [part_number=SEN-10245]
  S4 = Load Sensor - 50kg [part_number=SEN-10245]
  Mod2 = Raspberry Pi 4B

nets:
  VCC: Part2.VCC, Mod2.3V3
  GND: Part2.GND, Mod2.GND
  N1: Part2.DO/RX, Mod2.GPIO5
  N2: Part2.CK/TX, Mod2.GPIO6
  N3: Part2.E+, S4.R
  N4: Part2.E-, S1.R
  N5: Part2.A+, S2.R
  N6: Part2.A-, S3.R
  N7: S1.B, S3.B
  N8: S1.W, S2.W
  N9: S2.B, S4.B
  N10: S3.W, S4.W

notes:
  A-
  A+
  E+
  E-

custom parts:
  HX711 Weighing Sensor Module: HX711 is a precision 24-bit analog-to-digital converter (ADC) designed for weigh scales and industrial control applications to interface directly with a bridge sensor.
  Load Sensor - 50kg: Half-wheatstone bridge Load Cell modified from the Fritzing Repo This load sensor, sometimes called a strain gauge, is the same one found in digital bathroom scales (you know, the ones you use in January for your New Year's resolutions, and then forget about a month later). This sensor can measure up to about 110 pounds.
